# Fritzing sketch gaburevolver (saved by Fritzing 0.9.2b)
breadboards: 1

parts:
  Raspberry_Pi1 = Raspberry Pi (Model B)
  IC1 = MCP23017 I2C I/O Expander
  SW1_メインスイッチ = Pushbutton [package=THT]
  SW6_回転部 = Pushbutton [package=THT]
  SW7_トリガー = Pushbutton [package=THT]
  SW8_開口 = Pushbutton [package=THT]
  SW9_ミニティラ = Pushbutton [package=THT]
  SW10_ガブリカリバー = Pushbutton [package=THT]
  ガブリボルバーGND = STARBOARD_GND [package=starboard_ground_wide]  # not connected
  SW2上 = Pushbutton [package=THT]
  SW2中 = Pushbutton [package=THT]
  SW2下 = Pushbutton [package=THT]
  SW3上 = Pushbutton [package=THT]
  SW3中 = Pushbutton [package=THT]
  SW3下 = Pushbutton [package=THT]
  SW5上 = Pushbutton [package=THT]
  SW4上 = Pushbutton [package=THT]
  SW4中 = Pushbutton [package=THT]
  SW5中 = Pushbutton [package=THT]
  SW4下 = Pushbutton [package=THT]
  SW5下 = Pushbutton [package=THT]
  S1 = Toggle Switch [package=THT]
  SW1_OFF接点 = Pushbutton [package=THT]

nets:
  3V3: Raspberry_Pi1.3V3, IC1.VDD, IC1.RESET, S1.L2
  N1: Raspberry_Pi1.SDA, IC1.SDA
  N2: Raspberry_Pi1.SCL, IC1.SCL
  GND: Raspberry_Pi1.GND, IC1.VSS, IC1.A0, IC1.A1, IC1.A2
  N3: Raspberry_Pi1.#18, SW6_回転部.leg0
  N4: Raspberry_Pi1.#22, SW8_開口.leg0
  N5: Raspberry_Pi1.#23, SW9_ミニティラ.leg0
  N6: Raspberry_Pi1.#24, SW10_ガブリカリバー.leg0
  N7: Raspberry_Pi1.#25, SW7_トリガー.leg0
  N8: IC1.GPB0, SW5上.leg1
  N9: IC1.GPB1, SW4上.leg0
  N10: IC1.GPB2, SW5中.leg1
  N11: IC1.GPB3, SW4中.leg0
  N12: IC1.GPB4, SW5下.leg1
  N13: IC1.GPB5, SW4下.leg0
  N14: IC1.GPA0, SW3上.leg1
  N15: IC1.GPA1, SW2上.leg0
  N16: IC1.GPA2, SW3中.leg1
  N17: IC1.GPA3, SW2中.leg0
  N18: IC1.GPA4, SW3下.leg1
  N19: IC1.GPA5, SW2下.leg0
  N20: SW1_メインスイッチ.leg0, S1.COM
  N21: S1.L1, SW1_OFF接点.leg0

custom parts:
  Raspberry Pi (Model B): Raspberry Pi Single-board Computer, Model B
  MCP23017 I2C I/O Expander: The MCP23017 uses two i2c pins (these can be shared with other i2c devices), and in exchange gives you 16 general purpose pins. You can set each of 16 pins to be input, output, input with a pullup or open drain. There's even the ability to get an interrupt via an external pin when any of the inputs change so you don't have to keep polling the chip.
