# Fritzing sketch minityra (saved by Fritzing 0.9.2b)
breadboards: 1

parts:
  Raspberry_Pi1 = Raspberry Pi (Model B)
  IC1 = MCP23017 I2C I/O Expander
  SW4_アゴ = Pushbutton [package=THT]
  SW5_クルリンチョ = Pushbutton [package=THT]
  SW6_合体 = Pushbutton [package=THT]
  SW7_トリガー = Pushbutton [package=THT]
  SW8_横スイッチ = Pushbutton [package=THT]
  電池ボックス- = STARBOARD_GND [package=starboard_ground_wide]
  SW2-4 = Pushbutton [package=THT]
  SW2-2 = Pushbutton [package=THT]
  SW2-1 = Pushbutton [package=THT]
  SW3-1 = Pushbutton [package=THT]
  SW3-2 = Pushbutton [package=THT]
  SW3-4 = Pushbutton [package=THT]

nets:
  3V3: Raspberry_Pi1.3V3, IC1.VDD, IC1.RESET
  N1: Raspberry_Pi1.SDA, IC1.SDA
  N2: Raspberry_Pi1.SCL, IC1.SCL
  GND: Raspberry_Pi1.GND, IC1.VSS, IC1.A0, IC1.A1, IC1.A2, 電池ボックス-.MOUNT
  N3: Raspberry_Pi1.#18, SW4_アゴ.leg0
  N4: Raspberry_Pi1.#22, SW6_合体.leg0
  N5: Raspberry_Pi1.#23, SW7_トリガー.leg0
  N6: Raspberry_Pi1.#24, SW8_横スイッチ.leg0
  N7: Raspberry_Pi1.#25, SW5_クルリンチョ.leg0
  N8: IC1.GPA0, SW3-1.leg1
  N9: IC1.GPA1, SW2-4.leg0
  N10: IC1.GPA2, SW2-2.leg1, SW3-2.leg1
  N11: IC1.GPA3, SW2-2.leg0
  N12: IC1.GPA4, SW3-4.leg1
  N13: IC1.GPA5, SW2-1.leg0

notes:
  電池ボックス+

custom parts:
  Raspberry Pi (Model B): Raspberry Pi Single-board Computer, Model B
  MCP23017 I2C I/O Expander: The MCP23017 uses two i2c pins (these can be shared with other i2c devices), and in exchange gives you 16 general purpose pins. You can set each of 16 pins to be input, output, input with a pullup or open drain. There's even the ability to get an interrupt via an external pin when any of the inputs change so you don't have to keep polling the chip.
