# Fritzing sketch yokai-watch-dx (saved by Fritzing 0.9.3b)
breadboards: 1

parts:
  IC1 = IC, DIP package, 18 pins [chip_label=TBD62783APG]
  Raspberry_Pi1 = Raspberry Pi 2

nets:
  N1: IC1.pin1, Raspberry_Pi1.GPIO17
  N2: IC1.pin2, Raspberry_Pi1.GPIO18
  N3: IC1.pin3, Raspberry_Pi1.GPIO22
  N4: IC1.pin4, Raspberry_Pi1.GPIO23
  N5: IC1.pin10, Raspberry_Pi1.GND

notes:
  SW6 -
  SW5 -
  SW4 -
  SW3 -
  BATT -
  BATT +
